# Fritzing sketch BedLed (saved by Fritzing 0.9.3b)
circuit board: 3.80668cm x 3.39668cm
breadboards: 1

parts:
  Q1 = MOSFET-NCHANNEL [part_number=IRFZ44N package=to220v]
  IC2 = Voltage Regulator [part_number=LM7805 package=to220-igo]
  U1 = attiny85 [package=dip]
  LED = Screw terminal - 2 pins [package=THT]
  Power_plug = Power plug
  C2 = Ceramic Capacitor [capacitance=0.1µF package="100 mil [THT, multilayer]"]
  D1 = Schottky Diode 700mil [package="700 mil [THT]"]
  J2 = double row female pin header, 6 pins [form="♀ (female)"]
  Button_2 = screw terminal, 3 pins
  Button_1 = screw terminal, 3 pins
  C1 = Ceramic Capacitor [capacitance=0.33µF voltage=16V package="100 mil [THT, multilayer]"]
  J1 = male pin header, 2 pins [form="♂ (male)"]
  J3 = male pin header, 4 pins [form="♂ (male)"]

nets:
  N1: Q1.G, J1.pin2
  N2: Q1.D, LED.pin2
  GND: Q1.S, IC2.GND, U1.Pin_4, Power_plug.GND, C2.1, J2.pin4, Button_2.pin1, Button_1.pin1, C1.0, J3.pin1
  12V: IC2.IN, LED.pin1, D1.cathode, C1.1
  5V: IC2.OUT, U1.Pin_8, C2.0, J2.pin6, Button_2.pin3, Button_1.pin3, J3.pin4
  N3: U1.Pin_1, J2.pin3
  N4: U1.Pin_2, Button_2.pin2
  N5: U1.Pin_3, Button_1.pin2
  N6: U1.Pin_5, J2.pin5, J3.pin3
  N7: U1.Pin_6, J2.pin1, J1.pin1
  N8: U1.Pin_7, J2.pin2
  N9: Power_plug.VCC, D1.anode

notes:
  Power Management
  LED Control
  9-20V ≤3A
  PWR
  LED
  SENS
  Chris van Marle
  IN
  -
  +
  BedLed v1 - 2017
  Button 1
  Button 2
  ICSP
  RF Expansion

custom parts:
  Schottky Diode 700mil: A standard schottky barrier rectifier diode - 700mil
